// Logisim project Registers.circ as structural Verilog: 7 circuits, main circuit Register File
module Register_File (
  input  [4:0] RA,
  input  [4:0] RB,
  input  [31:0] Bus_W,
  input  [4:0] RW,
  input  RegWrite,
  output [31:0] Bus_A,
  output [31:0] Bus_B
);

  wire [11:0] n3x4_zipper_4_wide_1_out_4, n3x4_zipper_4_wide_1_out_5, n3x4_zipper_4_wide_1_out_6,
       n3x4_zipper_4_wide_1_out_7, n3x4_zipper_4_wide_2_out_4, n3x4_zipper_4_wide_2_out_5,
       n3x4_zipper_4_wide_2_out_6, n3x4_zipper_4_wide_2_out_7;
  wire [15:0] decoder_1_out0, decoder_1_out16, decoder_2_out0, decoder_2_out16, decoder_3_out0,
       decoder_3_out16;

  Decoder #(.select(5)) decoder_1 (
    .out0(decoder_1_out0[0]), .out1(decoder_1_out0[1]), .out2(decoder_1_out0[2]), .out3(decoder_1_out0[3]),
    .out4(decoder_1_out0[4]), .out5(decoder_1_out0[5]), .out6(decoder_1_out0[6]), .out7(decoder_1_out0[7]),
    .out8(decoder_1_out0[8]), .out9(decoder_1_out0[9]), .out10(decoder_1_out0[10]),
    .out11(decoder_1_out0[11]), .out12(decoder_1_out0[12]), .out13(decoder_1_out0[13]),
    .out14(decoder_1_out0[14]), .out15(decoder_1_out0[15]), .out16(decoder_1_out16[0]),
    .out17(decoder_1_out16[1]), .out18(decoder_1_out16[2]), .out19(decoder_1_out16[3]),
    .out20(decoder_1_out16[4]), .out21(decoder_1_out16[5]), .out22(decoder_1_out16[6]),
    .out23(decoder_1_out16[7]), .out24(decoder_1_out16[8]), .out25(decoder_1_out16[9]),
    .out26(decoder_1_out16[10]), .out27(decoder_1_out16[11]), .out28(decoder_1_out16[12]),
    .out29(decoder_1_out16[13]), .out30(decoder_1_out16[14]), .out31(decoder_1_out16[15]), .sel(RA));  // open: en
  Decoder #(.select(5)) decoder_2 (
    .out0(decoder_2_out0[0]), .out1(decoder_2_out0[1]), .out2(decoder_2_out0[2]), .out3(decoder_2_out0[3]),
    .out4(decoder_2_out0[4]), .out5(decoder_2_out0[5]), .out6(decoder_2_out0[6]), .out7(decoder_2_out0[7]),
    .out8(decoder_2_out0[8]), .out9(decoder_2_out0[9]), .out10(decoder_2_out0[10]),
    .out11(decoder_2_out0[11]), .out12(decoder_2_out0[12]), .out13(decoder_2_out0[13]),
    .out14(decoder_2_out0[14]), .out15(decoder_2_out0[15]), .out16(decoder_2_out16[0]),
    .out17(decoder_2_out16[1]), .out18(decoder_2_out16[2]), .out19(decoder_2_out16[3]),
    .out20(decoder_2_out16[4]), .out21(decoder_2_out16[5]), .out22(decoder_2_out16[6]),
    .out23(decoder_2_out16[7]), .out24(decoder_2_out16[8]), .out25(decoder_2_out16[9]),
    .out26(decoder_2_out16[10]), .out27(decoder_2_out16[11]), .out28(decoder_2_out16[12]),
    .out29(decoder_2_out16[13]), .out30(decoder_2_out16[14]), .out31(decoder_2_out16[15]), .sel(RB));  // open: en
  Decoder #(.select(5), .disabled(0)) decoder_3 (
    .out0(decoder_3_out0[0]), .out1(decoder_3_out0[1]), .out2(decoder_3_out0[2]), .out3(decoder_3_out0[3]),
    .out4(decoder_3_out0[4]), .out5(decoder_3_out0[5]), .out6(decoder_3_out0[6]), .out7(decoder_3_out0[7]),
    .out8(decoder_3_out0[8]), .out9(decoder_3_out0[9]), .out10(decoder_3_out0[10]),
    .out11(decoder_3_out0[11]), .out12(decoder_3_out0[12]), .out13(decoder_3_out0[13]),
    .out14(decoder_3_out0[14]), .out15(decoder_3_out0[15]), .out16(decoder_3_out16[0]),
    .out17(decoder_3_out16[1]), .out18(decoder_3_out16[2]), .out19(decoder_3_out16[3]),
    .out20(decoder_3_out16[4]), .out21(decoder_3_out16[5]), .out22(decoder_3_out16[6]),
    .out23(decoder_3_out16[7]), .out24(decoder_3_out16[8]), .out25(decoder_3_out16[9]),
    .out26(decoder_3_out16[10]), .out27(decoder_3_out16[11]), .out28(decoder_3_out16[12]),
    .out29(decoder_3_out16[13]), .out30(decoder_3_out16[14]), .out31(decoder_3_out16[15]), .sel(RW),
    .en(RegWrite));
  _3x4_Zipper__4_wide u_3x4_zipper_4_wide_1 (
    .RA(decoder_1_out16), .RB(decoder_2_out16), .RW(decoder_3_out16), .out_4(n3x4_zipper_4_wide_1_out_4),
    .out_5(n3x4_zipper_4_wide_1_out_5), .out_6(n3x4_zipper_4_wide_1_out_6), .out_7(n3x4_zipper_4_wide_1_out_7));
  Register_Cell register_cell_1 (
    .RA(n3x4_zipper_4_wide_1_out_4[3:0]), .RB(n3x4_zipper_4_wide_1_out_4[7:4]),
    .RW(n3x4_zipper_4_wide_1_out_4[11:8]), .BusW(Bus_W), .BusA(Bus_A), .BusB(Bus_B));
  Register_Cell register_cell_2 (
    .RA(n3x4_zipper_4_wide_1_out_5[3:0]), .RB(n3x4_zipper_4_wide_1_out_5[7:4]),
    .RW(n3x4_zipper_4_wide_1_out_5[11:8]), .BusW(Bus_W), .BusA(Bus_A), .BusB(Bus_B));
  Register_Cell register_cell_3 (
    .RA(n3x4_zipper_4_wide_1_out_6[3:0]), .RB(n3x4_zipper_4_wide_1_out_6[7:4]),
    .RW(n3x4_zipper_4_wide_1_out_6[11:8]), .BusW(Bus_W), .BusA(Bus_A), .BusB(Bus_B));
  Register_Cell register_cell_4 (
    .RA(n3x4_zipper_4_wide_1_out_7[3:0]), .RB(n3x4_zipper_4_wide_1_out_7[7:4]),
    .RW(n3x4_zipper_4_wide_1_out_7[11:8]), .BusW(Bus_W), .BusA(Bus_A), .BusB(Bus_B));
  Clock clock_1 ();  // open: out
  _3x4_Zipper__4_wide u_3x4_zipper_4_wide_2 (
    .RA(decoder_1_out0), .RB(decoder_2_out0), .RW(decoder_3_out0), .out_4(n3x4_zipper_4_wide_2_out_4),
    .out_5(n3x4_zipper_4_wide_2_out_5), .out_6(n3x4_zipper_4_wide_2_out_6), .out_7(n3x4_zipper_4_wide_2_out_7));
  Register_Cell_w__0 register_cell_w_0_1 (
    .RA(n3x4_zipper_4_wide_2_out_4[3:0]), .RB(n3x4_zipper_4_wide_2_out_4[7:4]),
    .RW(n3x4_zipper_4_wide_2_out_4[11:8]), .BusW(Bus_W), .BusA(Bus_A), .BusB(Bus_B));
  Register_Cell register_cell_5 (
    .RA(n3x4_zipper_4_wide_2_out_5[3:0]), .RB(n3x4_zipper_4_wide_2_out_5[7:4]),
    .RW(n3x4_zipper_4_wide_2_out_5[11:8]), .BusW(Bus_W), .BusA(Bus_A), .BusB(Bus_B));
  Register_Cell register_cell_6 (
    .RA(n3x4_zipper_4_wide_2_out_6[3:0]), .RB(n3x4_zipper_4_wide_2_out_6[7:4]),
    .RW(n3x4_zipper_4_wide_2_out_6[11:8]), .BusW(Bus_W), .BusA(Bus_A), .BusB(Bus_B));
  Register_Cell register_cell_7 (
    .RA(n3x4_zipper_4_wide_2_out_7[3:0]), .RB(n3x4_zipper_4_wide_2_out_7[7:4]),
    .RW(n3x4_zipper_4_wide_2_out_7[11:8]), .BusW(Bus_W), .BusA(Bus_A), .BusB(Bus_B));
endmodule

module Register_Cell (
  input  [3:0] RA,
  input  [3:0] RB,
  input  [3:0] RW,
  input  [31:0] BusW,
  output [31:0] BusA,
  output [31:0] BusB
);

  wire [2:0] n3x4_zipper_1_out_4, n3x4_zipper_1_out_5, n3x4_zipper_1_out_6, n3x4_zipper_1_out_7;

  Clock clock_1 ();  // open: out
  _3x4_zipper u_3x4_zipper_1 (
    .RA(RA), .RB(RB), .RW(RW), .out_4(n3x4_zipper_1_out_4), .out_5(n3x4_zipper_1_out_5),
    .out_6(n3x4_zipper_1_out_6), .out_7(n3x4_zipper_1_out_7));
  _32_bit_Register u_32_bit_register_1 (.BusW(BusW), .Control(n3x4_zipper_1_out_4), .BusA(BusA), .BusB(BusB));
  _32_bit_Register u_32_bit_register_2 (.BusW(BusW), .Control(n3x4_zipper_1_out_5), .BusA(BusA), .BusB(BusB));
  _32_bit_Register u_32_bit_register_3 (.BusW(BusW), .Control(n3x4_zipper_1_out_6), .BusA(BusA), .BusB(BusB));
  _32_bit_Register u_32_bit_register_4 (.BusW(BusW), .Control(n3x4_zipper_1_out_7), .BusA(BusA), .BusB(BusB));
endmodule

module Register_Cell_w__0 (
  input  [3:0] RA,
  input  [3:0] RB,
  input  [3:0] RW,
  input  [31:0] BusW,
  output [31:0] BusA,
  output [31:0] BusB
);

  wire [2:0] n3x4_zipper_1_out_4, n3x4_zipper_1_out_5, n3x4_zipper_1_out_6, n3x4_zipper_1_out_7;

  Clock clock_1 ();  // open: out
  _3x4_zipper u_3x4_zipper_1 (
    .RA(RA), .RB(RB), .RW(RW), .out_4(n3x4_zipper_1_out_4), .out_5(n3x4_zipper_1_out_5),
    .out_6(n3x4_zipper_1_out_6), .out_7(n3x4_zipper_1_out_7));
  _32_bit_0_Register u_32_bit_0_register_1 (.Control(n3x4_zipper_1_out_4), .BusA(BusA), .BusB(BusB));
  _32_bit_Register u_32_bit_register_1 (.BusW(BusW), .Control(n3x4_zipper_1_out_5), .BusA(BusA), .BusB(BusB));
  _32_bit_Register u_32_bit_register_2 (.BusW(BusW), .Control(n3x4_zipper_1_out_6), .BusA(BusA), .BusB(BusB));
  _32_bit_Register u_32_bit_register_3 (.BusW(BusW), .Control(n3x4_zipper_1_out_7), .BusA(BusA), .BusB(BusB));
endmodule

module _32_bit_Register (
  input  [31:0] BusW,
  input  [2:0] Control,
  output [31:0] BusA,
  output [31:0] BusB
);

  wire clock_1_out;
  wire [31:0] register_1_q;

  Clock clock_1 (.out(clock_1_out));
  Register #(.width(32)) register_1 (.D(BusW), .en(Control[2]), .Q(register_1_q), .clk(clock_1_out));  // open: clr
  assign BusA = Control[0] ? register_1_q : 32'bz;  // Controlled_Buffer controlled_buffer_1
  assign BusB = Control[1] ? register_1_q : 32'bz;  // Controlled_Buffer controlled_buffer_2
endmodule

module _32_bit_0_Register (
  input  [2:0] Control,
  output [31:0] BusA,
  output [31:0] BusB
);

  Clock clock_1 ();  // open: out
  assign BusA = Control[0] ? {32{1'b0}} : 32'bz;  // Controlled_Buffer controlled_buffer_1
  assign BusB = Control[1] ? {32{1'b0}} : 32'bz;  // Controlled_Buffer controlled_buffer_2
endmodule

module _3x4_zipper (
  input  [3:0] RA,
  input  [3:0] RB,
  input  [3:0] RW,
  output [2:0] out_4,
  output [2:0] out_5,
  output [2:0] out_6,
  output [2:0] out_7
);


  assign out_4 = {RW[0], RB[0], RA[0]};
  assign out_5 = {RW[1], RB[1], RA[1]};
  assign out_6 = {RW[2], RB[2], RA[2]};
  assign out_7 = {RW[3], RB[3], RA[3]};
endmodule

module _3x4_Zipper__4_wide (
  input  [15:0] RA,
  input  [15:0] RB,
  input  [15:0] RW,
  output [11:0] out_4,
  output [11:0] out_5,
  output [11:0] out_6,
  output [11:0] out_7
);


  assign out_4 = {RW[3:0], RB[3:0], RA[3:0]};
  assign out_5 = {RW[7:4], RB[7:4], RA[7:4]};
  assign out_6 = {RW[11:8], RB[11:8], RA[11:8]};
  assign out_7 = {RW[15:12], RB[15:12], RA[15:12]};
endmodule
